# Fritzing sketch TardisCircut (saved by Fritzing 0.9.1b)
breadboards: 1

parts:
  IC1 = WTV020SD [package=ssop_20]
  Rst = Pushbutton [package=THT]
  LED1 = RGB LED (com. cathode, rbg) [package="5 mm [THT]"]
  LED2 = RGB LED (com. cathode, rbg) [package="5 mm [THT]"]
  LED3 = RGB LED (com. cathode, rbg) [package="5 mm [THT]"]
  LED4 = RGB LED (com. cathode, rbg) [package="5 mm [THT]"]
  Top_LED = RGB LED (com. cathode, rbg) [package="5 mm [THT]"]
  Part1 = Arduino Nano (Rev3.0) (ICSP)
  SP1 = SPEAKER [package=pcb_mount_speaker]
  R2 = Resistor [tolerance=±5% resistance=100k package="0603 [SMD]"]
  R3 = Thermistor 100K [package=THT]

nets:
  N1: IC1.P04, Part1.D4
  N2: IC1.P05, Part1.D7
  N3: IC1.P06, Part1.D8
  VCC: IC1.VCC, Part1.3V3
  N4: IC1.SPK_P, SP1.-
  N5: IC1.SPK_N, SP1.+
  GND: IC1.GND, Rst.leg0, LED1.common_cathode, LED2.common_cathode, LED3.common_cathode, LED4.common_cathode, Top_LED.common_cathode, Part1.GND, R3.pin_0
  N6: IC1.RESET, Part1.D2
  N7: Rst.leg1, Part1.RESET
  N8: LED1.red_anode, LED2.red_anode, LED3.red_anode, LED4.red_anode, Part1.D3
  N9: LED1.blue_anode, LED2.blue_anode, LED3.blue_anode, LED4.blue_anode, Part1.D6
  N10: LED1.green_anode, LED2.green_anode, LED3.green_anode, LED4.green_anode, Part1.D5
  N11: Top_LED.red_anode, Part1.D9
  N12: Top_LED.blue_anode, Part1.D11/MOSI
  N13: Top_LED.green_anode, Part1.D10
  N14: Part1.5V, R2.Pin_1
  N15: Part1.A0, R2.Pin_0, R3.pin_1

custom parts:
  Thermistor 100K: A 100k NTC Thermistor (Temperature Sensor)
